# Fritzing sketch Sketch1 (saved by Fritzing 0.9.4)
breadboards: 1

parts:
  Part1 = Arduino Mega 2560 (Rev3)  # not connected
  Pololu_A1 = Pololu A4988 [package=SO16]
  LCD2004-I2C1 = LCD2004-I2C  # not connected
  kEYPAD_MATRICIAL_1 = KEYPAD 4x3  # not connected
  ZS-042_RTC1 = ZS-042 RTC Module  # not connected
  microSD1 = MicroSD Card Module  # not connected
  U1 = LIPO-2000mAh [package=lipo-2000]  # not connected
  M1 = Stepper Motor - Bipolar

nets:
  N1: Pololu_A1.VMOT, M1.A

custom parts:
  LCD2004-I2C: A standard character display with 4x20 characters. Comes in many colors with LCM2004 IIC attached.
  KEYPAD 4x3: KEYPAD matricial de 12 botones, 4 filas x 3 columnas
